# Fritzing sketch Wetterstation Platine (saved by Fritzing 0.9.6b)
circuit board: 7cm x 7cm

parts:
  R4 = Resistor [tolerance=±5% resistance=220 power=0.25 package=THT]
  R5 = Resistor [tolerance=±5% resistance=4.7k power=0.25 package=THT]
  R6 = Resistor [tolerance=±5% resistance=4.7k power=0.25 package=THT]
  WeMos_D1_Mini = WeMos D1 Mini
  DATA_LED = female pin header, 2 pins [form="♀ (female)"]
  DS18B20_1 = mystery part, 3 pins [chip_label=DS18B20]
  R8 = Resistor [tolerance=±5% resistance=4.7k power=0.25 package=THT]
  IC3 = V_REG_LD1117VXX [package=78xxl]
  3_3-30V_in = Screw terminal - 2 pins [package=THT]
  C5 = Electrolytic Capacitor [capacitance=10µF package="200 mil [THT, electrolytic]"]
  I2C = female pin header, 4 pins [form="♀ (female)"]
  I2C1 = female pin header, 4 pins [form="♀ (female)"]
  Regensensor = mystery part, 3 pins [chip_label=?]
  DS18B20_2 = mystery part, 3 pins [chip_label=DS18B20]
  I2C2 = female pin header, 4 pins [form="♀ (female)"]

nets:
  N1: R4.Pin_0, WeMos_D1_Mini.D8
  N2: R4.Pin_1, DATA_LED.pin1
  N3: R5.Pin_0, WeMos_D1_Mini.D2, I2C.pin2, I2C1.pin2, I2C2.pin2
  3.3V: R5.Pin_1, R6.Pin_1, WeMos_D1_Mini.3V3, DS18B20_1.pin1, R8.Pin_1, IC3.OUT, C5.+, I2C.pin3, I2C1.pin3, DS18B20_2.pin1, I2C2.pin3
  N4: R6.Pin_0, WeMos_D1_Mini.D1, I2C.pin1, I2C1.pin1, I2C2.pin1
  N5: WeMos_D1_Mini.A0, Regensensor.pin3
  WAKE: WeMos_D1_Mini.D0
  N6: WeMos_D1_Mini.D3, DS18B20_1.pin2, R8.Pin_0, DS18B20_2.pin2
  N7: WeMos_D1_Mini.D5, Regensensor.pin1
  GND: WeMos_D1_Mini.G, DATA_LED.pin2, DS18B20_1.pin3, IC3.GND, 3_3-30V_in.pin1, C5.-, I2C.pin4, I2C1.pin4, Regensensor.pin2, DS18B20_2.pin3, I2C2.pin4
  N8: IC3.IN, 3_3-30V_in.pin2

notes:
  WAKE
