# Fritzing sketch Wetterstation (saved by Fritzing 0.9.6b)
circuit board: 7cm x 7cm

parts:
  Bauteil6 = BH1750
  BME280 = BMP180 Breakout (GY-68)
  3_3-30V_in = Screw terminal - 2 pins [package=THT]
  LED1_DATA = LED - 5mm [color="Green (565nm)" current=0.030 package="5 mm [THT]"]
  R4 = Resistor [tolerance=±5% resistance=220 power=0.25 package=THT]
  R5 = Resistor [tolerance=±5% resistance=4.7k power=0.25 package=THT]
  R6 = Resistor [tolerance=±5% resistance=4.7k power=0.25 package=THT]
  WeMos_D1_Mini2 = WeMos D1 Mini
  DS18B20_1 = mystery part, 3 pins [chip_label=DS18B20]
  R7 = Resistor [tolerance=±5% resistance=4.7k power=0.25 package=THT]
  IC2 = V_REG_LD1117VXX [package=78xxl]
  C4 = Electrolytic Capacitor [capacitance=10µF package="100 mil [THT, electrolytic]"]
  DS18B20_2 = mystery part, 3 pins [chip_label=DS18B20]
  YL-83_-_Control_Board = YL-83 Rain Sensor - Control Board
  Regensensor = YL-83 Rain Sensor - Detection Board
  Bauteil7 = VEML6070 [part_number=VEML6070]

nets:
  3.3V: Bauteil6.VCC, BME280.VCC, R5.Pin_1, R6.Pin_1, WeMos_D1_Mini2.3V3, DS18B20_1.pin1, R7.Pin_1, IC2.OUT, C4.+, DS18B20_2.pin1, Bauteil7.VDD
  GND: Bauteil6.GND, BME280.GND, 3_3-30V_in.pin1, LED1_DATA.cathode, WeMos_D1_Mini2.G, DS18B20_1.pin3, IC2.GND, C4.-, DS18B20_2.pin3, YL-83_-_Control_Board.GND, Bauteil7.GND
  N1: Bauteil6.SCL, BME280.SCL, R6.Pin_0, WeMos_D1_Mini2.D1, Bauteil7.SCL
  N2: Bauteil6.SDA, BME280.SDA, R5.Pin_0, WeMos_D1_Mini2.D2, Bauteil7.SDA
  N3: 3_3-30V_in.pin2, IC2.IN
  N4: LED1_DATA.anode, R4.Pin_1
  N5: R4.Pin_0, WeMos_D1_Mini2.D8
  N6: WeMos_D1_Mini2.A0, YL-83_-_Control_Board.AO
  WAKE: WeMos_D1_Mini2.D0, WeMos_D1_Mini2.RST
  N7: WeMos_D1_Mini2.D3, DS18B20_1.pin2, R7.Pin_0, DS18B20_2.pin2
  N8: WeMos_D1_Mini2.D5, YL-83_-_Control_Board.VCC
  N9: YL-83_-_Control_Board.POS, Regensensor.POS
  N10: YL-83_-_Control_Board.NEG, Regensensor.NEG

notes:
  WAKE

custom parts:
  BH1750: Light Sensor
  BMP180 Breakout (GY-68): This is a simple breakout board for the BMP180, a high-precision, low-power barometric pressure sensor made by Bosch Sensortec. The range of measurement is from 300hPa to 1100hPa. The sensor can be supplied with voltage ranging from 1.8V to 3.6V. Operating temperature range is -40 to +85 °C. This particular breakout board (or perhaps the configuration) is produced by Shenzhen Keep Power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
  YL-83 Rain Sensor - Control Board: The YL-83 is a rain sensor that has more resistance when dry and less resistance when wet. The module runs at 5V.
  YL-83 Rain Sensor - Detection Board: The YL-83 is a rain sensor that has more resistance when dry and less resistance when wet. The module runs at 5V.
  VEML6070: This little sensor is a great way to add UV light sensing to any microcontroller project. The VEML6070 from Vishay has a true UV A light sensor and an I2C-controlled ADC that will take readings and integrate them for you over ~60ms to 500ms.
